# Fritzing sketch Untitled_Sketch (saved by Fritzing 0.9.3b)

parts:
  Composant1 = Arduino Uno (Rev3)  # not connected
  Composant2 = Base Shield V2
  Grove1 = Grove OLED 128x96
  Grove_Light_Sensor1 = Grove Light Sensor
  Grove2 = Grove Bar LED

nets:
  N1: Composant2.pin_96, Grove2.GND
  N2: Composant2.pin_97, Grove2.VCC
  N3: Composant2.pin_98, Grove2.DIO
  N4: Composant2.pin_99, Grove2.CLK
  N5: Composant2.pin_124, Grove1.GND
  N6: Composant2.pin_125, Grove1.VCC
  N7: Composant2.pin_126, Grove1.SDA
  N8: Composant2.pin_127, Grove1.SCL
  N9: Composant2.pin_140, Grove_Light_Sensor1.SIG
  N10: Composant2.pin_141, Grove_Light_Sensor1.NC
  N11: Composant2.pin_142, Grove_Light_Sensor1.VCC
  N12: Composant2.pin_143, Grove_Light_Sensor1.GND

custom parts:
  Grove Light Sensor: Light Sensor, Grove connector.
